# Fritzing sketch PCB (saved by Fritzing 0.9.3b)
circuit board: 6.4cm x 6.39604cm
breadboards: 1

parts:
  Arduino = Arduino Pro Mini v13
  7805 = Voltage Regulator - 5V [package="TO220 [THT]"]
  Drop = Header 3 [package=molex-1x3_lock]
  Radar = Header 3 [package=molex-1x3_lock]
  Light = Header 2 [package=molex-1x2_lock]
  Temperature = Header 4 [package=molex-1x4_lock]
  7404 = 7404 [package="DIP 14 [THT]"]
  Right = Header 4 [package=molex-1x4_lock]
  Front = Header 4 [package=molex-1x4_lock]
  Left = Header 4 [package=molex-1x4_lock]
  Right_2 = Header 3 [package=molex-1x3_lock]
  Left_2 = Header 3 [package=molex-1x3_lock]
  Power = Header 2 [package=screwterminal-3.5mm-2_lock]
  Serial = Header 4 [package=molex-1x4_lock]
  LED = Header 2 [package=molex-1x2_lock]

nets:
  N1: Arduino.D0/TX, Serial.4
  N2: Arduino.D1/RX, Serial.3
  N3: Arduino.VCC, Serial.2
  GND: Arduino.GND, 7805.GND, Drop.3, Radar.3, Temperature.4, 7404.GND, Right.4, Front.4, Left.4, Power.2, Serial.1, LED.2
  N4: Arduino.A4, Temperature.3
  N5: Arduino.A5, Temperature.2
  N6: Arduino.A3, Light.2
  N7: Arduino.A2, Right.3
  N8: Arduino.A1, Right.2
  N9: Arduino.A0, Front.3
  N10: Arduino.D13/SCK, Front.2
  N11: Arduino.D12/MISO, Left.3
  N12: Arduino.D11_PWM/MOSI, Left.2
  N13: Arduino.D10_PWM/SS, Drop.2
  N14: Arduino.D9_PWM, Radar.2
  N15: Arduino.D8, LED.1
  N16: Arduino.D7, 7404.6A, Left_2.3
  N17: Arduino.D6_PWM, Left_2.1
  N18: Arduino.D3_PWM, Right_2.1
  N19: 7805.input_voltage, Power.1
  N20: 7805.output_voltage, Drop.1, Radar.1, Light.1, Temperature.1, 7404.VCC, Right.1, Front.1, Left.1
  N21: 7404.3A, Right_2.2
  N22: 7404.3Y, Right_2.3
  N23: 7404.6Y, Left_2.2

custom parts:
  7404: Hex inverter
