# Fritzing sketch breadboard (saved by Fritzing 0.9.3b)
circuit board: 2.88407cm x 1.07245cm
circuit board: 17.5783cm x 8.69586cm
breadboards: 1

parts:
  Raspberry_Pi_1 = Raspberry Pi B rev2
  Componente1 = Arduino Pro Mini v13
  S1 = H-Bridge with L298N
  S2 = H-Bridge with L298N
  M1 = DC Motor
  M2 = DC Motor
  M3 = DC Motor
  M4 = DC Motor
  U1 = LIPO-2000mAh [package=lipo-2000]
  U2 = LIPO-2000mAh [package=lipo-2000]
  U3 = Voltage Regulator - 5V [package="DPak [SMD]"]
  U4 = MLX90614 [package=to-39]
  C1 = Ceramic Capacitor [capacitance=0.1µF package="100 mil [THT, multilayer]"]
  Componente2 = SRF05 Ultrasonic Rangefinder
  Componente3 = SRF05 Ultrasonic Rangefinder
  Componente4 = SRF05 Ultrasonic Rangefinder
  J1 = Basic Servo
  7404 = 7404 [package="DIP 14 [THT]"]
  J2 = Basic Servo
  R2 = Photocell (LDR) [package=THT]
  USB1 = Wiring USB Adapter

nets:
  VCC: Raspberry_Pi_1.5V, U3.output_voltage, U4.VDD, C1.1, Componente2.VCC, Componente3.VCC, Componente4.VCC, J1.vcc, 7404.VCC, J2.vcc, R2.pin_1
  GND: Raspberry_Pi_1.GND, S1.12V, S1.GND, S2.GND, U2.-, U3.GND, U4.VSS, C1.0, Componente2.GND, Componente3.GND, Componente4.GND, J1.gnd, 7404.GND, J2.gnd
  N1: Raspberry_Pi_1.GPIO_14, Componente1.D1/RX, USB1.TX
  N2: Raspberry_Pi_1.GPIO_15, Componente1.D0/TX, USB1.RX
  VCC_2: Componente1.VCC, USB1.5V
  GND_2: Componente1.GND, USB1.GND
  N3: Componente1.A0, R2.pin_0
  N4: Componente1.D13/SCK, S1.IN2, S1.IN4, 7404.2A
  N5: Componente1.D12/MISO, S2.IN2, S2.IN4, 7404.3A
  N6: Componente1.D11_PWM/MOSI, S2.ENA, S2.ENB
  N7: Componente1.D10_PWM/SS, S1.ENA, S1.ENB
  N8: Componente1.D9_PWM, J1.pulse
  N9: Componente1.D8, J2.pulse
  N10: Componente1.D7, Componente2.Echo
  N11: Componente1.D6_PWM, Componente2.Trig
  N12: Componente1.D5_PWM, Componente3.Echo
  N13: Componente1.D4, Componente3.Trig
  N14: Componente1.D3_PWM, Componente4.Echo
  N15: Componente1.D2, Componente4.Trig
  N16: S1.IN1, S1.IN3, 7404.2Y
  N17: S1.M1-01, M3.pin_2
  N18: S1.M1-02, M3.pin_1
  N19: S1.M2-01, S2.M1-02, M1.pin_1, M4.pin_2
  N20: S1.M2-02, M4.pin_1
  N21: S2.12V, U1.+, U3.input_voltage
  N22: S2.IN1, S2.IN3, 7404.3Y
  N23: S2.M1-01, M1.pin_2
  N24: S2.M2-01, M2.pin_2
  N25: S2.M2-02, M2.pin_1
  N26: U1.-, U2.+

custom parts:
  H-Bridge with L298N: h-bridge
  7404: Hex inverter
